// Logisim project Project_1.circ as structural Verilog: 1 circuit, main circuit main
module main (
  input  A,
  input  B,
  input  C
);

  wire and_1_out, and_2_out, and_3_out, and_4_out, and_5_out, nand_1_out, nand_2_out, nand_3_out, nand_4_out,
       nand_5_out, nand_6_out, nand_7_out, nand_8_out, nand_9_out, nand_10_out, not_A_out, not_B_out,
       not_C_out;

  not not_A (not_A_out, A);
  not not_B (not_B_out, B);
  not not_C (not_C_out, C);
  nand nand_1 (nand_1_out, A, B, C);
  nand nand_2 (nand_2_out, not_A_out, B, C);
  nand nand_3 (nand_3_out, A, not_B_out, not_C_out);
  nand nand_4 (nand_4_out, A, not_B_out, C);
  nand nand_5 (nand_5_out, not_A_out, not_B_out, C);
  and and_1 (and_1_out, A, B, C);
  and and_2 (and_2_out, not_A_out, B, C);
  and and_3 (and_3_out, A, not_B_out, not_C_out);
  and and_4 (and_4_out, A, not_B_out, C);
  and and_5 (and_5_out, not_A_out, not_B_out, C);
  nand nand_6 (nand_6_out, nand_1_out, nand_1_out);
  nand nand_7 (nand_7_out, nand_2_out, nand_2_out);
  nand nand_8 (nand_8_out, nand_3_out, nand_3_out);
  nand nand_9 (nand_9_out, nand_4_out, nand_4_out);
  nand nand_10 (nand_10_out, nand_5_out, nand_5_out);
  // OR_Gate or_1 has open pins: in0=and_1_out, in1=and_2_out, in2=and_3_out, in3=and_4_out, in4=and_5_out, out=open
  // OR_Gate or_2 has open pins: in0=nand_6_out, in1=nand_7_out, in2=nand_8_out, in3=nand_9_out, in4=nand_10_out, out=open
endmodule
